# Fritzing sketch rpm_sensor (saved by Fritzing 0.9.3b)

parts:
  Part1 = Adafruit Pro Trinket 5V 16MHz [part_number="Adafruit #2000"]
  R1 = Resistor [tolerance=±5% resistance=10k package=THT]
  D1 = Rectifier Diode [part_number=1N4001 package="300 mil [THT]"]
  U1 = mystery part, 3 pins [chip_label=SS443R part_number=SS443R]

nets:
  N1: Part1.GND, U1.pin2
  N2: Part1.+5V, R1.Pin_1, U1.pin1
  N3: Part1.D3, R1.Pin_0, D1.anode
  N4: D1.cathode, U1.pin3

custom parts:
  Adafruit Pro Trinket 5V 16MHz: Trinket's got a big sister in town - the Pro Trinket 5V! Pro Trinket combines everything you love about Trinket with the familiarity of the common core Arduino chip, the ATmega328. It's like an Arduino Pro Mini with more pins and USB tossed in, so delicious. Trinket's a year old now, and while its been great to see tons of tiny projects, sometimes you just need more pins, more FLASH, and more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
